# Fritzing sketch BlueHello (saved by Fritzing 1.0.4)
breadboards: 1

parts:
  RHT1 = Humidity and Temperature Sensor RHT03
  Part1 = Arduino Mega 2560 (Rev3)
  LED2 = LED - 5mm [color="Green (570nm)" current=0.030A package="5 mm [THT]"]
  R1 = Resistor [tolerance=±5% resistance=220 package="2512 [SMD]"]
  BT1 = Bluetooth HC-06u [package=THT]
  R3 = Resistor [tolerance=±5% resistance=10k package="2512 [SMD]"]
  R4 = Resistor [tolerance=±5% resistance=1k package="2512 [SMD]"]
  R5 = Resistor [tolerance=±5% resistance=2.2k package="2512 [SMD]"]

nets:
  VCC: RHT1.Vcc, Part1.5V, BT1.VCC
  N1: RHT1.Data-signal, R3.Pin_0
  GND: RHT1.GND_2, Part1.GND, LED2.anode, BT1.GND, R5.Pin_0
  N2: Part1.D19/RX1, BT1.TXD
  N3: Part1.D18/TX1, R4.Pin_0, R5.Pin_1
  N4: Part1.D13_PWM, R1.Pin_1
  N5: Part1.D7_PWM, R3.Pin_1
  N6: LED2.cathode, R1.Pin_0
  N7: BT1.RXD, R4.Pin_1

custom parts:
  Bluetooth HC-06u: Bluetooth HC-06 - face up, pins down 16.5mm x 37.5mm PCB
